# Fritzing sketch ONE (saved by Fritzing 0.9.3b)
circuit board: 9.00001cm x 7.40001cm

parts:
  HLK-PM1 = HLK-PM01
  BME = female pin header, 4 pins [form="♀ (female)"]
  J1 = screw terminal, 6 pins
  Raspberry_Pi_Zero_W = Raspberry Pi Zero
  J8 = shrouded pin header, 26 pins [form="♂ (shrouded male)"]

nets:
  N1: HLK-PM1.AC#0, J1.pin2
  N2: HLK-PM1.AC#1, J1.pin1
  N3: HLK-PM1.+Vo, Raspberry_Pi_Zero_W.pin_2, Raspberry_Pi_Zero_W.pin_4, J8.pin12, J8.pin13
  N4: BME.pin1, Raspberry_Pi_Zero_W.pin_3, J8.pin15
  N5: BME.pin2, Raspberry_Pi_Zero_W.pin_5, J8.pin16
  N6: BME.pin4, Raspberry_Pi_Zero_W.pin_1, Raspberry_Pi_Zero_W.pin_17, J8.pin14, J8.pin22
  N7: Raspberry_Pi_Zero_W.pin_6, Raspberry_Pi_Zero_W.pin_9, Raspberry_Pi_Zero_W.pin_14, Raspberry_Pi_Zero_W.pin_20, Raspberry_Pi_Zero_W.pin_25, Raspberry_Pi_Zero_W.pin_30, Raspberry_Pi_Zero_W.pin_34, Raspberry_Pi_Zero_W.pin_39, J8.pin4, J8.pin7, J8.pin11, J8.pin18, J8.pin26
  N8: Raspberry_Pi_Zero_W.pin_7, J8.pin17
  N9: Raspberry_Pi_Zero_W.pin_8, J8.pin10
  N10: Raspberry_Pi_Zero_W.pin_10, J8.pin9
  N11: Raspberry_Pi_Zero_W.pin_11, J8.pin19
  N12: Raspberry_Pi_Zero_W.pin_12, J8.pin8
  N13: Raspberry_Pi_Zero_W.pin_13, J8.pin20
  N14: Raspberry_Pi_Zero_W.pin_15, J8.pin21
  N15: Raspberry_Pi_Zero_W.pin_16, J8.pin6
  N16: Raspberry_Pi_Zero_W.pin_18, J8.pin5
  N17: Raspberry_Pi_Zero_W.pin_19, J8.pin23
  N18: Raspberry_Pi_Zero_W.pin_21, J8.pin24
  N19: Raspberry_Pi_Zero_W.pin_22, J8.pin3
  N20: Raspberry_Pi_Zero_W.pin_23, J8.pin25
  N21: Raspberry_Pi_Zero_W.pin_24, J8.pin2
  N22: Raspberry_Pi_Zero_W.pin_26, J8.pin1

notes:
  RESET
  +5V
  GND
  AC L
  AC N
  PSU
  C(N)
  R(L)
  W(W)
  Y(H)
  G(Hum)
  W2
  L - AC IN - N
  N - AC IN - L
  GND  +5V DC
  +5V DC  GND
  BME
  Vin
  SCL
  SDA
  Raspberry Pi Zero W
  RL1      W(W)
  RL2     Y (H)
  RL3    G (Hum)
  RL4      W2
  (Hum): Humidity
  (L): AC Live
  (W): Hot Water
  (H): Heating
  W2: 2-stage Heating
  (N): AC Neutral
  W (WHITE): Heating
  Y (YELLOW): Cooling
  C (BL): Common
  R (RED): 24V AC
  HVAC Model
  G (GREEN): Fan
  ( EU Model )
  31
  3
  8
  7
  15
  13
  18
  35
  26
  37
  19
  16
  5
  11
  36
  32
  33
  10
  12
  28
  24
  23
  5V
  29
  21
  27
  22
  3V3
  38
  40
  www.hestiapi.com
  HestiaPi Touch ONE
  .
  < LCD
  RL1-W(W)
  RL2-Y(H)
  RL3-G(H)
  RL4-W2
